// Logisim project BLOQUE_B.circ as structural Verilog: 1 circuit, main circuit BLOQUE_B
module BLOQUE_B (
  input  GH,
  input  PH,
  input  GL,
  input  PL,
  input  Cin,
  output GHL,
  output PHL,
  output CH,
  output CL
);

  wire and_1_out, and_3_out;

  and and_1 (and_1_out, PH, GL);
  or or_1 (GHL, GH, and_1_out);
  and and_2 (PHL, PH, PL);
  and and_3 (and_3_out, PL, Cin);
  or or_2 (CH, and_3_out, GL);

  assign CL = Cin;
endmodule
