// Logisim project Carry_De_Salida.circ as structural Verilog: 1 circuit, main circuit Carry_De_Salida
module Carry_De_Salida (
  input  GL,
  input  PL,
  input  Cin,
  output CH
);

  wire and_1_out;

  and and_1 (and_1_out, PL, Cin);
  or or_1 (CH, GL, and_1_out);
endmodule
