// Logisim project Comparador48.circ as structural Verilog: 1 circuit, main circuit Comparador48
module Comparador48 (
  input  [7:0] EstadoActual,
  output es_48
);

  wire and_1_out, and_2_out, and_3_out, and_4_out, and_5_out, and_6_out, not_1_out, not_2_out, not_3_out,
       not_4_out, not_5_out, not_6_out;

  not not_1 (not_1_out, EstadoActual[0]);
  not not_2 (not_2_out, EstadoActual[1]);
  not not_3 (not_3_out, EstadoActual[2]);
  not not_4 (not_4_out, EstadoActual[3]);
  not not_5 (not_5_out, EstadoActual[6]);
  not not_6 (not_6_out, EstadoActual[7]);
  and and_1 (and_1_out, not_1_out, not_2_out);
  and and_2 (and_2_out, not_3_out, not_4_out);
  and and_3 (and_3_out, EstadoActual[4], EstadoActual[5]);
  and and_4 (and_4_out, not_5_out, not_6_out);
  and and_5 (and_5_out, and_1_out, and_2_out);
  and and_6 (and_6_out, and_3_out, and_4_out);
  and and_7 (es_48, and_5_out, and_6_out);
endmodule
