// Logisim project Comparador55.circ as structural Verilog: 1 circuit, main circuit Comparador55
module Comparador55 (
  input  [7:0] EstadoActual,
  output es_55
);

  wire and_1_out, and_2_out, and_3_out, and_4_out, and_5_out, and_6_out, not_1_out, not_2_out, not_3_out;

  not not_1 (not_1_out, EstadoActual[3]);
  not not_2 (not_2_out, EstadoActual[6]);
  not not_3 (not_3_out, EstadoActual[7]);
  and and_1 (and_1_out, EstadoActual[0], EstadoActual[1]);
  and and_2 (and_2_out, EstadoActual[2], not_1_out);
  and and_3 (and_3_out, EstadoActual[4], EstadoActual[5]);
  and and_4 (and_4_out, not_2_out, not_3_out);
  and and_5 (and_5_out, and_1_out, and_2_out);
  and and_6 (and_6_out, and_3_out, and_4_out);
  and and_7 (es_55, and_5_out, and_6_out);
endmodule
