// Logisim project Contador.circ as structural Verilog: 1 circuit, main circuit Contador_8bits
module Contador_8bits (
  input  Reset,
  input  Z1,
  input  Z2,
  input  Z3,
  input  Z4,
  input  A,
  input  B,
  input  C,
  input  D,
  input  E,
  output Enable,
  output LoadAlternativo,
  output Load,
  output [7:0] Data
);

  wire and_2_out, CLK_out, comparador0_1_es_0, comparador48_1_es_48, comparador49_1_es_49,
       comparador50_1_es_50, comparador51_1_es_51, comparador52_1_es_52, comparador55_1_es_55,
       modo_alternativo_1_modoalternativo, not_1_out, or_1_out, or_2_out, or_4_out;
  wire [3:0] binary_to_bcd_converter_1_p2, binary_to_bcd_converter_1_p3, binary_to_bcd_converter_1_p4;
  wire [7:0] counter_1_q, sumlat_1_suma;

  Comparador48 comparador48_1 (.EstadoActual(counter_1_q), .es_48(comparador48_1_es_48));
  Comparador49 comparador49_1 (.EstadoActual(counter_1_q), .es_49(comparador49_1_es_49));
  Comparador50 comparador50_1 (.EstadoActual(counter_1_q), .es_50(comparador50_1_es_50));
  Comparador51 comparador51_1 (.EstadoActual(counter_1_q), .es_51(comparador51_1_es_51));
  MODO_ALTERNATIVO modo_alternativo_1 (
    .Z1(Z1), .Z2(Z2), .Z3(Z3), .Z4(Z4), .A(A), .B(B), .C(C), .D(D), .E(E),
    .ModoAlternativo(modo_alternativo_1_modoalternativo));
  Comparador52 comparador52_1 (.EstadoActual(counter_1_q), .es_52(comparador52_1_es_52));
  Comparador55 comparador55_1 (.EstadoActual(counter_1_q), .es_55(comparador55_1_es_55));
  Comparador0 comparador0_1 (.EstadoActual(counter_1_q), .es_0(comparador0_1_es_0));
  or or_1 (or_1_out, comparador48_1_es_48, comparador49_1_es_49);
  SUMLAT sumlat_1 (.A(counter_1_q), .B(8'h3), .C0(1'b0), .SUMA(sumlat_1_suma));  // open: Cout
  or or_2 (or_2_out, comparador48_1_es_48, comparador49_1_es_49);
  not not_1 (not_1_out, modo_alternativo_1_modoalternativo);
  and and_1 (LoadAlternativo, or_1_out, modo_alternativo_1_modoalternativo);
  or or_3 (Load, LoadAlternativo, comparador52_1_es_52, comparador55_1_es_55, comparador0_1_es_0);
  or or_4 (or_4_out, comparador55_1_es_55, comparador0_1_es_0);
  and and_2 (and_2_out, or_2_out, not_1_out);
  Multiplexer #(.width(8)) multiplexer_1 (.in0(sumlat_1_suma), .in1(8'h30), .out(Data), .sel(or_4_out));
  or or_5 (Enable, and_2_out, comparador50_1_es_50, comparador51_1_es_51);
  Clock CLK (.out(CLK_out));
  Counter counter_1 (
    .clr(Reset), .load(Load), .up(1'b1), .count(Enable), .clk(CLK_out), .D(Data), .Q(counter_1_q));  // open: carry
  Hex_Digit_Display hex_digit_display_1 (.value(binary_to_bcd_converter_1_p2));  // open: dp
  // Binary_to_BCD_converter #(.binvalue(8)) binary_to_bcd_converter_1: pin names not known; wires that end beside it: counter_1_q, binary_to_bcd_converter_1_p2, binary_to_bcd_converter_1_p3, binary_to_bcd_converter_1_p4
  Hex_Digit_Display hex_digit_display_2 (.value(binary_to_bcd_converter_1_p3));  // open: dp
  Hex_Digit_Display hex_digit_display_3 (.value(binary_to_bcd_converter_1_p4));  // open: dp

  // Notes on the sheet:
  //   Constante = 48
endmodule
