// Logisim project F1.circ as structural Verilog: 1 circuit, main circuit F_1
module F_1 (
  input  Z1,
  input  Z2,
  input  Z3,
  input  Z4,
  output F1
);

  ROM #(.addrWidth(4), .dataWidth(1)) rom_1 (.addr({Z4, Z3, Z2, Z1}));  // open: data

  // Notes on the sheet:
  //   contents of rom_1 (hex, n*v repeats v):
  //   1 1 0 1 0 0 0 1 0 1 1 0 0 1 0 1
endmodule
