// Logisim project FAGP.circ as structural Verilog: 1 circuit, main circuit FAGP
module FAGP (
  input  Ai,
  input  Bi,
  input  Cin,
  output S,
  output P,
  output G
);

  wire xor_1_out;

  xor xor_1 (xor_1_out, Ai, Bi);
  or or_1 (P, Ai, Bi);
  and and_1 (G, Ai, Bi);
  xor xor_2 (S, xor_1_out, Cin);
endmodule
