// Logisim project ModoAlternativo.circ as structural Verilog: 1 circuit, main circuit MODO_ALTERNATIVO
module MODO_ALTERNATIVO (
  input  Z1,
  input  Z2,
  input  Z3,
  input  Z4,
  input  A,
  input  B,
  input  C,
  input  D,
  input  E,
  output ModoAlternativo
);

  wire f_1_1_f1, f_2_1_f2;

  F_1 f_1_1 (.Z1(Z1), .Z2(Z2), .Z3(Z3), .Z4(Z4), .F1(f_1_1_f1));
  F_2 f_2_1 (.A(A), .B(B), .C(C), .D(D), .E(E), .F2(f_2_1_f2));
  and and_1 (ModoAlternativo, f_1_1_f1, f_2_1_f2);
endmodule
