// Logisim project SUMLAT.circ as structural Verilog: 1 circuit, main circuit SUMLAT
module SUMLAT (
  input  [7:0] A,
  input  [7:0] B,
  input  C0,
  output [7:0] SUMA,
  output Cout
);

  wire bloque_b_1_ch, bloque_b_1_cl, bloque_b_1_ghl, bloque_b_1_phl, bloque_b_2_ch, bloque_b_2_cl,
       bloque_b_2_ghl, bloque_b_2_phl, bloque_b_3_ch, bloque_b_3_cl, bloque_b_3_ghl, bloque_b_3_phl,
       bloque_b_4_ch, bloque_b_4_cl, bloque_b_4_ghl, bloque_b_4_phl, bloque_b_5_ch, bloque_b_5_cl,
       bloque_b_5_ghl, bloque_b_5_phl, bloque_b_6_ch, bloque_b_6_cl, bloque_b_6_ghl, bloque_b_6_phl,
       bloque_b_7_ch, bloque_b_7_cl, bloque_b_7_ghl, bloque_b_7_phl, fagp_1_g, fagp_1_p, fagp_2_g, fagp_2_p,
       fagp_3_g, fagp_3_p, fagp_4_g, fagp_4_p, fagp_5_g, fagp_5_p, fagp_6_g, fagp_6_p, fagp_7_g, fagp_7_p,
       fagp_8_g, fagp_8_p;

  FAGP fagp_1 (.Ai(A[7]), .Bi(B[7]), .Cin(bloque_b_1_ch), .S(SUMA[7]), .P(fagp_1_p), .G(fagp_1_g));
  BLOQUE_B bloque_b_1 (
    .GH(fagp_1_g), .PH(fagp_1_p), .GL(fagp_2_g), .PL(fagp_2_p), .Cin(bloque_b_2_ch), .GHL(bloque_b_1_ghl),
    .PHL(bloque_b_1_phl), .CH(bloque_b_1_ch), .CL(bloque_b_1_cl));
  BLOQUE_B bloque_b_2 (
    .GH(bloque_b_1_ghl), .PH(bloque_b_1_phl), .GL(bloque_b_4_ghl), .PL(bloque_b_4_phl), .Cin(bloque_b_3_ch),
    .GHL(bloque_b_2_ghl), .PHL(bloque_b_2_phl), .CH(bloque_b_2_ch), .CL(bloque_b_2_cl));
  BLOQUE_B bloque_b_3 (
    .GH(bloque_b_2_ghl), .PH(bloque_b_2_phl), .GL(bloque_b_6_ghl), .PL(bloque_b_6_phl), .Cin(C0),
    .GHL(bloque_b_3_ghl), .PHL(bloque_b_3_phl), .CH(bloque_b_3_ch), .CL(bloque_b_3_cl));
  FAGP fagp_2 (.Ai(A[6]), .Bi(B[6]), .Cin(bloque_b_1_cl), .S(SUMA[6]), .P(fagp_2_p), .G(fagp_2_g));
  Carry_De_Salida carry_de_salida_1 (.GL(bloque_b_3_ghl), .PL(bloque_b_3_phl), .Cin(C0), .CH(Cout));
  FAGP fagp_3 (.Ai(A[5]), .Bi(B[5]), .Cin(bloque_b_4_ch), .S(SUMA[5]), .P(fagp_3_p), .G(fagp_3_g));
  BLOQUE_B bloque_b_4 (
    .GH(fagp_3_g), .PH(fagp_3_p), .GL(fagp_4_g), .PL(fagp_4_p), .Cin(bloque_b_2_cl), .GHL(bloque_b_4_ghl),
    .PHL(bloque_b_4_phl), .CH(bloque_b_4_ch), .CL(bloque_b_4_cl));
  FAGP fagp_4 (.Ai(A[4]), .Bi(B[4]), .Cin(bloque_b_4_cl), .S(SUMA[4]), .P(fagp_4_p), .G(fagp_4_g));
  FAGP fagp_5 (.Ai(A[3]), .Bi(B[3]), .Cin(bloque_b_5_ch), .S(SUMA[3]), .P(fagp_5_p), .G(fagp_5_g));
  BLOQUE_B bloque_b_5 (
    .GH(fagp_5_g), .PH(fagp_5_p), .GL(fagp_6_g), .PL(fagp_6_p), .Cin(bloque_b_6_ch), .GHL(bloque_b_5_ghl),
    .PHL(bloque_b_5_phl), .CH(bloque_b_5_ch), .CL(bloque_b_5_cl));
  BLOQUE_B bloque_b_6 (
    .GH(bloque_b_5_ghl), .PH(bloque_b_5_phl), .GL(bloque_b_7_ghl), .PL(bloque_b_7_phl), .Cin(bloque_b_3_cl),
    .GHL(bloque_b_6_ghl), .PHL(bloque_b_6_phl), .CH(bloque_b_6_ch), .CL(bloque_b_6_cl));
  FAGP fagp_6 (.Ai(A[2]), .Bi(B[2]), .Cin(bloque_b_5_cl), .S(SUMA[2]), .P(fagp_6_p), .G(fagp_6_g));
  FAGP fagp_7 (.Ai(A[1]), .Bi(B[1]), .Cin(bloque_b_7_ch), .S(SUMA[1]), .P(fagp_7_p), .G(fagp_7_g));
  BLOQUE_B bloque_b_7 (
    .GH(fagp_7_g), .PH(fagp_7_p), .GL(fagp_8_g), .PL(fagp_8_p), .Cin(bloque_b_6_cl), .GHL(bloque_b_7_ghl),
    .PHL(bloque_b_7_phl), .CH(bloque_b_7_ch), .CL(bloque_b_7_cl));
  FAGP fagp_8 (.Ai(A[0]), .Bi(B[0]), .Cin(bloque_b_7_cl), .S(SUMA[0]), .P(fagp_8_p), .G(fagp_8_g));
endmodule
