// Logisim project TesterDelCircuito.circ as structural Verilog: 1 circuit, main circuit main
module main (
  input  [7:0] A,
  input  [7:0] B,
  input  Carry_Entrada,
  output [7:0] Resultado,
  output Carry_Salida
);

  SUMLAT sumlat_1 (.A(A), .B(B), .C0(Carry_Entrada), .SUMA(Resultado), .Cout(Carry_Salida));
endmodule
